# Fritzing sketch Phate PCB Mk35 Final Upload (saved by Fritzing 0.9.6b)
circuit board: 5.4cm x 8.5cm

parts:
  Arduino_Nano_3_2 = Arduino Nano (Rev3.0) [part_number="Nano 3.2"]
  Air = screw terminal, 2 pins
  Water = screw terminal, 2 pins
  Buzzer = mystery part, 3 pins [chip_label=Buzzer]
  Power_In_12V_DC = Power Jack [part_number="12V DC" package=power_jack_pth]
  Panel_Switches = mystery part, 10 pins [chip_label=Switches]
  LCD = mystery part, 4 pins [chip_label=LCD]
  Relay_Board = mystery part, 6 pins [chip_label="Relay Board"]
  Air_2 = Resistor [tolerance=±5% power=0.25 resistance=10k package=THT]
  Water_2 = Resistor [tolerance=±5% power=0.25 resistance=10k package=THT]
  Light = Resistor [tolerance=±5% power=0.25 resistance=10k package=THT]
  Start = Resistor [tolerance=±5% power=0.25 resistance=10k package=THT]
  Stop = Resistor [tolerance=±5% power=0.25 resistance=10k package=THT]
  Emerg = Resistor [tolerance=±5% power=0.25 resistance=10k package=THT]
  DC/DC_LM2596 = LM2596 Haydn
  Pad1 = Circle Image  # not connected
  Water_Switch_Bypass = mystery part, 3 pins [chip_label="Water Switch Bypass"]
  Air_Switch_Bypass = mystery part, 3 pins [chip_label="Air Switch Bypass"]

nets (from the schematic view):
  GND: Arduino_Nano_3_2.GND, Buzzer.pin3, Panel_Switches.pin10, LCD.pin1, Relay_Board.pin2, Air_2.Pin_1, Water_2.Pin_1, Light.Pin_0, Start.Pin_0, Stop.Pin_0, Emerg.Pin_0
  Light: Arduino_Nano_3_2.D4, Panel_Switches.pin2, Light.Pin_1
  Buzzer: Arduino_Nano_3_2.D5, Buzzer.pin1
  Start: Arduino_Nano_3_2.D6, Panel_Switches.pin4, Start.Pin_1
  Stop: Arduino_Nano_3_2.D7, Panel_Switches.pin6, Stop.Pin_1
  Emergency: Arduino_Nano_3_2.D8, Panel_Switches.pin8, Emerg.Pin_1
  Water: Arduino_Nano_3_2.D9, Water.pin2, Water_2.Pin_0, Water_Switch_Bypass.pin1
  Air: Arduino_Nano_3_2.D10, Air.pin2, Air_2.Pin_0, Air_Switch_Bypass.pin1
  5V: Arduino_Nano_3_2.5V, Buzzer.pin2, Panel_Switches.pin1, Panel_Switches.pin3, Panel_Switches.pin5, Panel_Switches.pin7, Panel_Switches.pin9, LCD.pin2, Relay_Board.pin1, Water_Switch_Bypass.pin2, Air_Switch_Bypass.pin2
  LCD CLK: Arduino_Nano_3_2.A5, LCD.pin3
  LCD DATA: Arduino_Nano_3_2.A4, LCD.pin4
  Relay 4: Arduino_Nano_3_2.A3, Relay_Board.pin6
  Relay 3: Arduino_Nano_3_2.A2, Relay_Board.pin5
  Relay 2: Arduino_Nano_3_2.A1, Relay_Board.pin4
  Relay 1: Arduino_Nano_3_2.A0, Relay_Board.pin3
  N1: Air.pin1, Air_Switch_Bypass.pin3
  N2: Water.pin1, Water_Switch_Bypass.pin3
  12V IN Negative: Power_In_12V_DC.GND, DC/DC_LM2596.IN-, DC/DC_LM2596.OUT+
  12V IN Positive: Power_In_12V_DC.PWR, DC/DC_LM2596.IN+

notes:
  Pin Numbers:
  Light Pin 4
  Start Pin 6
  Stop Pin 7
  Emergency Pin 8
  Water 9
  Air 10
  LCD - CLK A5
  LCD - DATA A4
  Relay 2 - Air A1
  Relay 4 - Heat Plate A3
  Relay 3 - Pump A2
  Relay 1 - Light A0
  Buzzer 5
  + -
  - +
  1
  2
  4
  3
  Mk1
  2021
  Phate
  Made by Haydn
  For Dennis @ Home Electrics
  https://github.com/Phateless/Home-Electrics
  Phate_less@telstra.com
  Relay 1 - Light
  Relay 2 - Fan
  Relay 3 - Pump
  Relay 4 - Heat Plates
  CLK
  DAT
  Power Out 5V DC
  Light Switch - 4
  Stop Switch - 7
  Start   Switch - 6
  Emergency - 8
  Light
  Start
  Stop
  Emergency
  Relay 1 - A0
  Relay 2 - A1
  Relay 3 - A2
  Relay 4 - A3
  Air Switch Pin - 10
  Water Switch - 9
  -  +  S
  Pin - 5
  Fume Cabinet
  Controller
  Bypass
  Power In 12V DC
  5V
  Switch

custom parts:
  LM2596 Haydn: LM2596 DC-DC Step Down Power Supply Module 3 A.
  Circle Image: Solder Mask Keepout-12mm
